// Logisim project TN1.circ as structural Verilog: 1 circuit, main circuit main
module main (
  input  A,
  input  B,
  input  C,
  output NAND,
  output NOR,
  output AND,
  output OR,
  output NOT,
  output XOR,
  output XNOR,
  output XOR3,
  output NAND3,
  output X,
  output CHAIN
);

  nand nand_1 (NAND, B, A);
  nor nor_1 (NOR, B, A);
  and and_1 (AND, B, A);
  or or_1 (OR, B, A);
  not not_1 (NOT, A);
  xor xor_1 (XOR, B, A);
  xnor xnor_1 (XNOR, B, A);
  xor xor_2 (XOR3, C, B, A);
  nand nand_2 (NAND3, C, B, A);
  and and_2 (X, B, A);
  nand nand_3 (CHAIN, X, C);
endmodule
