// Logisim project TN2.circ as structural Verilog: 1 circuit, main circuit main
module main (
  input  x,
  input  y,
  input  z,
  output EQ1,
  output EQ2,
  output EQ3,
  output EQ4,
  output EQ5
);

  wire and_1_out, and_2_out, and_3_out, and_4_out, and_5_out, and_6_out, and_7_out, not_1_out, not_2_out,
       not_3_out, not_4_out, not_5_out, not_6_out, not_7_out, not_8_out, or_1_out, or_2_out, or_3_out,
       or_4_out, or_5_out, or_6_out, or_7_out;

  not not_1 (not_1_out, x);
  not not_2 (not_2_out, x);
  not not_3 (not_3_out, y);
  not not_4 (not_4_out, x);
  not not_5 (not_5_out, y);
  not not_6 (not_6_out, x);
  or or_1 (or_1_out, y, x);
  not not_7 (not_7_out, or_1_out);
  and and_1 (and_1_out, not_3_out, not_4_out);
  and and_2 (and_2_out, y, x);
  not not_8 (not_8_out, and_2_out);
  and and_3 (and_3_out, not_5_out, not_6_out);
  and and_4 (and_4_out, y, z);
  or or_2 (or_2_out, y, x);
  or or_3 (or_3_out, z, x);
  and and_5 (and_5_out, y, not_1_out);
  and and_6 (and_6_out, y, not_2_out);
  or or_4 (or_4_out, x, and_4_out);
  and and_7 (and_7_out, or_2_out, or_3_out);
  or or_5 (or_5_out, and_5_out, x);
  or or_6 (or_6_out, and_6_out, x);
  or or_7 (or_7_out, y, x);
  xnor xnor_1 (EQ1, not_7_out, and_1_out);
  xnor xnor_2 (EQ2, not_8_out, and_3_out);
  xnor xnor_3 (EQ3, or_4_out, and_7_out);
  xnor xnor_4 (EQ4, or_5_out, x);
  xnor xnor_5 (EQ5, or_6_out, or_7_out);
endmodule
