// Logisim project Warmup.circ as structural Verilog: 1 circuit, main circuit main
module main (
  input  A,
  input  B,
  output f
);

  wire not_1_out;

  and and_1 (f, A, not_1_out);
  not not_1 (not_1_out, B);
endmodule
